# Fritzing sketch Untitled Sketch (saved by Fritzing 0.9.4)

parts:
  U1 = NodeMCU V1.0
  M1 = MAX30100
  M2 = Max30205 body temp sensor [package=THT]

nets:
  N1: U1.D1, M1.SCL, M2.SCL
  N2: U1.D2, M1.SDA, M2.SDA
  GND: U1.GND, M1.GND
  VIN: U1.Vin, M1.VIN, M2.VCC

custom parts:
  NodeMCU V1.0: ESP8266 based NodeMCU
  MAX30100: Oximeter module using the MAX30100 chip. You may wish to read (and check your module) this post on power problems with these modules: https://reedpaper.wordpress.com/2018/08/22/pulse-oximeter-max30100-max30102-how-to-fix-wrong-board/ . As usual, if you want the mounting holes in pcb, you need to drag a hole over the pad in silkscreen to actually drill the hole (by default they are not drilled)
  Max30205 body temp sensor: This module is based on MAX30205 which is a temperature sensor that accurately measures temperature and provides an over-temperature alarm/interrupt/shutdown output.
